# Fritzing sketch Class-02_Ultrasonic_Sensors (saved by Fritzing 0.8.5b)
breadboards: 1

parts:
  LED1 = LED - 5mm [color="Red (633nm)" package="5 mm [THT]"]
  Part1 = SRF05 Ultrasonic Rangefinder
  Arduino1 = Arduino Uno (Rev3)

nets:
  GND: LED1.cathode, Part1.GND, Arduino1.GND
  N1: LED1.anode, Arduino1.D13/SCK
  N2: Part1.Trig, Arduino1.D4
  N3: Part1.Echo, Arduino1.D3_PWM

notes:
  Echo needs to connect to PWM pin
