# Fritzing sketch Class-04-PushButton_Buzzer (saved by Fritzing 0.8.5b)
breadboards: 1

parts:
  S1 = Pushbutton [package="[THT]"]
  J1 = Piezo Speaker
  Arduino1 = Arduino Uno (Rev3)
  R3 = Resistor [tolerance=±5% resistance=10k package=THT]
  R2 = Resistor [tolerance=±5% resistance=100 package=THT]

nets:
  N1: S1.Pin_1, S1.Pin_2, Arduino1.D2, R3.Pin_0
  N2: S1.Pin_3, S1.Pin_4, Arduino1.5V
  N3: J1.pin1, Arduino1.GND, R3.Pin_1
  N4: J1.pin2, R2.Pin_1
  N5: Arduino1.D11_PWM/MOSI, R2.Pin_0
