# Fritzing sketch Class-05_Temp_LCD (saved by Fritzing 0.8.5b)
breadboards: 1

parts:
  Part1 = Arduino Uno (Rev3)
  LCD1 = LCD screen  # not connected
  DHT1 = DHT11 Humitidy and Temperature Sensor
  JP1 = Header 4 [package=jst-4-pth]
  R1 = Resistor [tolerance=±5% resistance=10k package=THT]

nets:
  N1: Part1.A4/SDA, JP1.3
  N2: Part1.A5/SCL, JP1.4
  N3: Part1.D13/SCK, DHT1.DATA, R1.Pin_1
  GND: Part1.GND, DHT1.GND, JP1.1
  5V: Part1.5V, DHT1.VDD, JP1.2, R1.Pin_0

notes:
  GND
  VCC
  SDA
  SCL
  SDA connects to A4
  SCL connects to A5
  Data
  10K pull up resistor

custom parts:
  DHT11 Humitidy and Temperature Sensor: DHT11 Humidity and Temperature Sensor
