# Fritzing sketch Class-13_RGB_LED (saved by Fritzing 0.8.5b)
circuit board: 1.24052cm x 5.33337cm
breadboards: 1

parts:
  Part1 = Arduino Uno (Rev3)
  270 = Resistor [tolerance=±5% resistance=270 package=THT]
  270_2 = Resistor [tolerance=±5% resistance=270 package=THT]
  270_3 = Resistor [tolerance=±5% resistance=270 package=THT]
  cathode = RGB LED (com. cathode, rbg) [package="5 mm [THT]"]

nets:
  N1: Part1.D9_PWM, 270_3.Pin_1
  N2: Part1.D10_PWM/SS, 270_2.Pin_1
  N3: Part1.D11_PWM/MOSI, 270.Pin_1
  N4: Part1.GND, cathode.common_cathode
  N5: 270.Pin_0, cathode.red_anode
  N6: 270_2.Pin_0, cathode.blue_anode
  N7: 270_3.Pin_0, cathode.green_anode

notes:
  If the RGB LED is a common cathode the longest pin connects to GND, for common anode, the pin connects to +5V
